# Fritzing sketch USBLCD (saved by Fritzing 0.9.3b)
breadboards: 1

parts:
  IC1 = MICROCONTROLLER [package=dil28-3-simon]
  S1 = Momentary Switch [package=ksa_sealed_tac_switch]
  C1 = Ceramic Capacitor [capacitance=100nF package="100 mil [THT, multilayer]"]
  Y1 = CRYSTAL [package=hc49u-v]  # not connected
  C2 = Capacitor [package=cap-pth-small2]
  C3 = Capacitor [package=cap-pth-small2]
  X1 = USB Connectors [package=usb-a-pcb]
  U1 = DIODE-ZENER [package=diode-zener]
  U2 = DIODE-ZENER [package=diode-zener]
  1Mohm = Resistor [tolerance=±5% resistance=220 package="0805 [SMD]"]
  1K5 = Resistor [tolerance=±5% resistance=220 package="2010 [SMD]"]
  68 = Resistor [tolerance=±5% resistance=220 package="2512 [SMD]"]
  68_2 = Resistor [tolerance=±5% resistance=220 package="2512 [SMD]"]
  C4 = Capacitor Polarized [package=cpol-radial-100uf-25v]
  U3 = LCD-16X2 [package=lcd-8x2]
  R1 = Trimmer Potentiometer [maximum_resistance=10kΩ package=THT]

nets:
  N1: IC1.PD2(INT0), 68_2.Pin_1
  N2: IC1.PD4(XCK_T0), 68.Pin_1
  VCC: IC1.VCC, C1.1, X1.VBUS, 1K5.Pin_1, U3.VDD, U3.A, R1.leg2
  GND: IC1.GND, S1.1, C1.0, C2.2, C3.2, X1.GND, C4.-, U3.VSS, U3.K, R1.leg1
  N3: IC1.PB0(ICP), U3.DB4
  N4: IC1.PB1(OC1A), U3.DB5
  N5: IC1.PB2(SS_OC1B), U3.DB6
  N6: IC1.PB3(MOSI_OC2), U3.DB7
  N7: IC1.PB4(MISO), U3.RS
  N8: IC1.PC2(ADC2), U3.R_W
  N9: IC1.PC3(ADC3), U3.E
  N10: X1.D-, U1.C, 1K5.Pin_0, 68.Pin_0
  N11: X1.D+, U2.C, 1Mohm.Pin_1, 68_2.Pin_0
  N12: U3.VO, R1.wiper
